# Fritzing sketch Microview C64 WiFi Cart R57 1v1 (saved by Fritzing 0.9.2b)
circuit board: 5.66585cm x 9.77512cm
breadboards: 1

parts:
  MicroView = MicroView [part_number=MicroView package="16pin wide"]
  RN-XV_Wi-Fi_Module = XBee
  MicroView_Breakout = female pin header, 16 pins [form="♀ (female)"]
  1 = Pad [width=3.03585894193728 height=6.87308646450179 connect=center]
  Reset = Pushbutton [package="[THT]"]
  TX = male pin header, 2 pins [form="♂ (male)"]
  RX = male pin header, 2 pins [form="♂ (male)"]
  Reset_2 = Pushbutton [package="[THT]"]
  1_2 = single row smd female pin header, 1 pin [form="♀ (female)"]
  2 = single row smd female pin header, 1 pin [form="♀ (female)"]
  3 = single row smd female pin header, 1 pin [form="♀ (female)"]
  12 = single row smd female pin header, 1 pin [form="♀ (female)"]
  U2 = PNP-Transistor [part_number=MCP1700 package="TO92 [THT]"]
  3_2 = Pad [width=3.03585894193728 height=6.87308646450179 connect=center]
  4 = Pad [width=3.03585894193728 height=6.87308646450179 connect=center]  # not connected
  2_2 = Pad [width=3.03585894193728 height=6.87308646450179 connect=center]
  5 = Pad [width=3.03585894193728 height=6.87308646450179 connect=center]  # not connected
  6 = Pad [width=3.03585894193728 height=6.87308646450179 connect=center]
  7 = Pad [width=3.03585894193728 height=6.87308646450179 connect=center]  # not connected
  8 = Pad [width=3.03585894193728 height=6.87308646450179 connect=center]  # not connected
  9 = Pad [width=3.03585894193728 height=6.87308646450179 connect=center]  # not connected
  10 = Pad [width=3.03585894193728 height=6.87308646450179 connect=center]  # not connected
  11 = Pad [width=3.03585894193728 height=6.87308646450179 connect=center]  # not connected
  12_2 = Pad [width=3.03585894193728 height=6.87308646450179 connect=center]
  VIN = 2.1mm DC Barrel Jack
  N = Pad [width=3.03585894193728 height=6.87308646450179 connect=center]
  B = Pad [width=3.03585894193728 height=6.87308646450179 connect=center]
  C = Pad [width=3.03585894193728 height=6.87308646450179 connect=center]
  D = Pad [width=3.03585894193728 height=6.87308646450179 connect=center]
  E = Pad [width=3.03585894193728 height=6.87308646450179 connect=center]
  F = Pad [width=3.03585894193728 height=6.87308646450179 connect=center]
  H = Pad [width=3.03585894193728 height=6.87308646450179 connect=center]
  J = Pad [width=3.03585894193728 height=6.87308646450179 connect=center]
  K = Pad [width=3.03585894193728 height=6.87308646450179 connect=center]
  L = Pad [width=3.03585894193728 height=6.87308646450179 connect=center]
  M = Pad [width=3.03585894193728 height=6.87308646450179 connect=center]
  D_2 = single row smd female pin header, 1 pin [form="♀ (female)"]
  M_2 = single row smd female pin header, 1 pin [form="♀ (female)"]
  A = single row smd female pin header, 1 pin [form="♀ (female)"]
  H_2 = single row smd female pin header, 1 pin [form="♀ (female)"]
  F_2 = single row smd female pin header, 1 pin [form="♀ (female)"]
  C_2 = single row smd female pin header, 1 pin [form="♀ (female)"]
  Reset_3 = Pushbutton [package="[THT]"]
  E_2 = single row smd female pin header, 1 pin [form="♀ (female)"]
  L_2 = single row smd female pin header, 1 pin [form="♀ (female)"]
  B_2 = single row smd female pin header, 1 pin [form="♀ (female)"]
  J_2 = single row smd female pin header, 1 pin [form="♀ (female)"]
  K_2 = single row smd female pin header, 1 pin [form="♀ (female)"]
  N_2 = single row smd female pin header, 1 pin [form="♀ (female)"]
  4116R-1-331LF = IC, DIP package, 16 pins [chip_label=IC]
  A_2 = Pad [width=3.03585894193728 height=6.87308646450179 connect=center]  # not connected
  Pad1 = Pad [width=5.22210362219904 height=1.7 connect=center]  # not connected
  UP9600 = male pin header, 2 pins [form="♂ (male)"]
  5_2 = single row smd female pin header, 1 pin [form="♀ (female)"]
  6_2 = single row smd female pin header, 1 pin [form="♀ (female)"]
  7_2 = single row smd female pin header, 1 pin [form="♀ (female)"]
  UP5V = male pin header, 2 pins [form="♂ (male)"]
  C1 = Capacitor [package=cap-pth-small-kit]
  UP9600-5 = male pin header, 2 pins [form="♂ (male)"]

nets:
  N1: MicroView.RESET, MicroView_Breakout.pin1, Reset_2.Pin_1
  RTS: MicroView.A5, MicroView_Breakout.pin2, 4116R-1-331LF.pin10
  DTR: MicroView.A4, MicroView_Breakout.pin3, 4116R-1-331LF.pin11
  RI: MicroView.A3, MicroView_Breakout.pin4, 4116R-1-331LF.pin12
  DCD: MicroView.A2, MicroView_Breakout.pin5, 4116R-1-331LF.pin13
  CTS: MicroView.A1, MicroView_Breakout.pin6, 4116R-1-331LF.pin14
  DSR: MicroView.A0, MicroView_Breakout.pin7, 4116R-1-331LF.pin15
  GND: MicroView.GND, RN-XV_Wi-Fi_Module.GND, MicroView_Breakout.pin8, 1.pad, Reset.Pin_3, Reset.Pin_4, Reset_2.Pin_3, Reset_2.Pin_4, 1_2.pin1, 12.pin1, U2.E, 12_2.pad, VIN.switch, VIN.sleeve, N.pad, A.pin1, Reset_3.Pin_3, Reset_3.Pin_4, N_2.pin1, C1.2
  N2: MicroView.RXD, RN-XV_Wi-Fi_Module.pin2, MicroView_Breakout.pin9, RX.pin1
  N3: MicroView.TXD, RN-XV_Wi-Fi_Module.pin3, MicroView_Breakout.pin10, TX.pin1
  N4: MicroView.D2, RN-XV_Wi-Fi_Module.pin12, MicroView_Breakout.pin11
  N5: MicroView.D3, RN-XV_Wi-Fi_Module.pin16, MicroView_Breakout.pin12
  TxD: MicroView.D5, MicroView_Breakout.pin13, TX.pin2, 4116R-1-331LF.pin16
  RxD: MicroView.D6, MicroView_Breakout.pin14, RX.pin2, 4116R-1-331LF.pin9
  5V: MicroView.5V, MicroView_Breakout.pin15, U2.B, UP5V.pin1
  VIN: MicroView.Vin, MicroView_Breakout.pin16, VIN.center
  3.3V: RN-XV_Wi-Fi_Module.VCC, U2.C, C1.1
  N6: RN-XV_Wi-Fi_Module.pin5, Reset.Pin_1
  N7: 2.pin1, 2_2.pad, UP5V.pin2
  N8: 3.pin1, 3_2.pad, Reset_3.Pin_1, Reset_3.Pin_2
  N9: 6.pad, UP9600.pin1, 6_2.pin1
  N10: B.pad, C.pad, C_2.pin1, B_2.pin1, 4116R-1-331LF.pin8, 7_2.pin1
  N11: D.pad, D_2.pin1, 4116R-1-331LF.pin7
  N12: E.pad, E_2.pin1, 4116R-1-331LF.pin6
  N13: F.pad, F_2.pin1, 4116R-1-331LF.pin5
  N14: H.pad, H_2.pin1, 4116R-1-331LF.pin4
  N15: J.pad, J_2.pin1
  N16: K.pad, K_2.pin1, 4116R-1-331LF.pin3
  N17: L.pad, L_2.pin1, 4116R-1-331LF.pin2, UP9600.pin2
  N18: M.pad, M_2.pin1, 4116R-1-331LF.pin1, UP9600-5.pin1
  N19: 5_2.pin1, UP9600-5.pin2

notes:
  RESET
  A5 SCL
  A4 SDA
  A3
  A2
  A1
  A0
  GND
  D0 RxD
  D2
  D3
  D5
  D6
  +5V
  VIN
  Top
  1
  16
  Commodore 64 - MicroView - Wi-Fi Modem
  Leif Bloomquist  2016  1v1
  Wi-Fi
  Test
  Signals to C64 User Port
  WIFI_CTS
  WIFI_RTS
  TX
  RX
  Jumpers to connect C64 directly to RN-XV if MicroView not present
  WIFI_TX
  WIFI_RX
  Actual C64 User Port
  MicroView
  Current Limiting Resistor Network
  Note pinout swapped!
  See MCP-1700 Datasheet
  Assumptions:
  C64 5V is clean/stable enough to use as 5V directly
  (doesn't have to be through VIN)
  C64
  D1 TxD
  C64_RX
  C64_TX
  -RxD-
  -RTS-
  -DTR-
  -RI-
  -DCD-
  -CTS-
  -DSR-
  -TxD-
  U1
  Other Side Up!
  Serial#
  www.jammingsignal.com
  Jumper to disconnect 5V from User Port

custom parts:
  MicroView: MicroView - Chip-sized Arduino with OLED display.
  2.1mm DC Barrel Jack: 2.1mm DC Barrel Jack with Thru-Hole Connectors (breadboardable)
